// Logisim project cache.circ as structural Verilog: 10 circuits, main circuit MCU
module MCU (
  input  [31:0] PC,
  input  [31:0] Address,
  input  [31:0] Data_In,
  input  Write,
  input  Select,
  input  Clock,
  input  [2:0] Mode,
  output Wait_for_Instruction,
  output [31:0] Next_Instruction,
  output Wait_for_Data,
  output [31:0] Data_Out
);

  wire and_1_out, clock_1_out, comparator_1_eq, s_r_ff_1_qn;
  wire [31:0] adder_1_out, multiplexer_1_out, n32bit_increment_1_out, register_1_q, register_2_q;

  Clock clock_1 (.out(clock_1_out));
  Multiplexer #(.width(32), .disabled(0), .enable("false")) multiplexer_1 (
    .in0(n32bit_increment_1_out), .in1(PC), .out(multiplexer_1_out), .sel(s_r_ff_1_qn));
  L1_Cache l1_cache_1 (
    .Address(PC), .Mode(3'b100), .Clock(clock_1_out), .Write(1'b0), .Data_Out(Next_Instruction),
    .Cache_miss(Wait_for_Instruction), .Enable(1'b1));  // open: Data_in, Load_Address, Load_Data
  L1_Cache l1_cache_2 (
    .Address(Address), .Data_in(Data_In), .Mode(Mode), .Clock(clock_1_out), .Write(Write),
    .Data_Out(Data_Out), .Cache_miss(Wait_for_Data), .Enable(Select));  // open: Load_Address, Load_Data
  _32bit_increment u_32bit_increment_1 (.In(register_1_q), .Out(n32bit_increment_1_out));
  Register #(.width(32)) register_1 (.D(multiplexer_1_out), .Q(register_1_q), .clk(clock_1_out));  // open: en, clr
  Register #(.width(32)) register_2 (.D(PC), .en(s_r_ff_1_qn), .Q(register_2_q), .clk(clock_1_out));  // open: clr
  and and_1 (and_1_out, Wait_for_Instruction, ~comparator_1_eq);  // AND_Gate
  Adder #(.width(32)) adder_1 (.a(register_2_q), .b(32'h100), .out(adder_1_out));  // open: cin, cout
  S_R_Flip_Flop s_r_ff_1 (
    .S(and_1_out), .clk(clock_1_out), .R(comparator_1_eq), .Qn(s_r_ff_1_qn));  // open: Q, preset, reset, en
  Comparator #(.width(32)) comparator_1 (.a(register_1_q), .b(adder_1_out), .eq(comparator_1_eq));  // open: gt, lt

  // Notes on the sheet:
  //   I-Cache
  //   D-Cache
endmodule

module Cache_Line (
  input  Write,
  input  Set_Tag,
  input  Clock,
  input  [31:0] Address,
  input  Sel,
  input  [2:0] Mode,
  input  [31:0] Data_In,
  output Hit,
  output [31:0] Data_Out
);

  wire and_2_out, and_3_out, and_4_out, and_5_out, and_6_out, and_7_out, comparator_1_eq, decoder_1_out0,
       decoder_1_out1, decoder_1_out2, decoder_1_out3, decoder_2_out0, decoder_2_out1, decoder_2_out2,
       or_1_out, or_2_out, or_3_out, or_4_out, or_5_out, or_6_out, or_7_out, s_r_ff_1_q;
  wire [4:0] multiplexer_1_out;
  wire [7:0] conditional_increment_1_output, conditional_increment_2_output, conditional_increment_3_output,
       multiplexer_2_out, ram_1_data, ram_2_data, ram_3_data, ram_4_data;
  wire [15:0] multiplexer_3_out;
  wire [21:0] Tag_q;
  wire [31:0] bit_extender_1_out, bit_extender_2_out, multiplexer_4_out, shifter_1_out;

  or or_1 (or_1_out, Write, Set_Tag);
  Decoder #(.select(2), .disabled(0)) decoder_1 (
    .out0(decoder_1_out0), .out1(decoder_1_out1), .out2(decoder_1_out2), .out3(decoder_1_out3),
    .sel(Address[1:0]), .en(Sel));
  Decoder #(.select(2), .enable("false")) decoder_2 (
    .out0(decoder_2_out0), .out1(decoder_2_out1), .out2(decoder_2_out2), .sel(Mode[2:1]));  // open: out3
  S_R_Flip_Flop s_r_ff_1 (.S(Set_Tag), .clk(Clock), .Q(s_r_ff_1_q));  // open: R, Qn, preset, reset, en
  Register #(.width(22)) Tag (.D(Address[31:10]), .en(Set_Tag), .Q(Tag_q), .clk(Clock));  // open: clr
  or or_2 (or_2_out, decoder_1_out2, decoder_1_out3);
  Multiplexer #(.select(2), .width(5), .enable("false")) multiplexer_1 (
    .in0({5{1'b0}}), .in1(5'b01000), .in2(5'b10000), .in3(5'b11000), .out(multiplexer_1_out),
    .sel(Address[1:0]));
  and and_1 (Hit, s_r_ff_1_q, comparator_1_eq);
  Comparator #(.width(22)) comparator_1 (.a(Tag_q), .b(Address[31:10]), .eq(comparator_1_eq));  // open: gt, lt
  or or_3 (or_3_out, decoder_1_out1, decoder_1_out2, decoder_1_out3);
  Shifter #(.width(32)) shifter_1 (.in(Data_In), .\dist (multiplexer_1_out), .out(shifter_1_out));
  or or_4 (or_4_out, decoder_1_out0, decoder_2_out2, and_2_out);
  and and_2 (and_2_out, decoder_2_out1, decoder_1_out3);
  or or_5 (or_5_out, decoder_1_out1, decoder_2_out2, and_3_out);
  and and_3 (and_3_out, decoder_2_out1, decoder_1_out0);
  or or_6 (or_6_out, decoder_1_out2, decoder_2_out2, and_4_out);
  and and_4 (and_4_out, decoder_2_out1, decoder_1_out1);
  or or_7 (or_7_out, decoder_1_out3, decoder_2_out2, and_5_out);
  and and_5 (and_5_out, decoder_2_out1, decoder_1_out2);
  conditional_increment conditional_increment_1 (
    .\input (Address[9:2]), .\output (conditional_increment_1_output), .inc(or_3_out));
  conditional_increment conditional_increment_2 (
    .\input (Address[9:2]), .\output (conditional_increment_2_output), .inc(or_2_out));
  conditional_increment conditional_increment_3 (
    .\input (Address[9:2]), .\output (conditional_increment_3_output), .inc(decoder_1_out3));
  RAM #(.bus("separate")) ram_1 (
    .addr(conditional_increment_1_output), .din(shifter_1_out[7:0]), .data(ram_1_data), .str(or_1_out),
    .sel(or_4_out), .clk(Clock));  // open: ld, clr
  RAM #(.bus("separate")) ram_2 (
    .addr(conditional_increment_2_output), .din(shifter_1_out[15:8]), .data(ram_2_data), .str(or_1_out),
    .sel(or_5_out), .clk(Clock));  // open: ld, clr
  RAM #(.bus("separate")) ram_3 (
    .addr(conditional_increment_3_output), .din(shifter_1_out[23:16]), .data(ram_3_data), .str(or_1_out),
    .sel(or_6_out), .clk(Clock));  // open: ld, clr
  RAM #(.bus("separate")) ram_4 (
    .addr(Address[9:2]), .din(shifter_1_out[31:24]), .data(ram_4_data), .str(or_1_out), .sel(or_7_out),
    .clk(Clock));  // open: ld, clr
  Multiplexer #(.select(2), .width(8), .enable("false")) multiplexer_2 (
    .in0(ram_1_data), .in1(ram_2_data), .in2(ram_3_data), .in3(ram_4_data), .out(multiplexer_2_out),
    .sel(Address[1:0]));
  Multiplexer #(.select(2), .width(16), .enable("false")) multiplexer_3 (
    .in0({ram_2_data, ram_1_data}), .in1({ram_3_data, ram_2_data}), .in2({ram_4_data, ram_3_data}),
    .in3({ram_1_data, ram_4_data}), .out(multiplexer_3_out), .sel(Address[1:0]));
  Multiplexer #(.select(2), .width(32), .enable("false")) multiplexer_4 (
    .in0({ram_4_data, ram_3_data, ram_2_data, ram_1_data}),
    .in1({ram_3_data, ram_2_data, ram_1_data, ram_4_data}),
    .in2({ram_2_data, ram_1_data, ram_4_data, ram_3_data}),
    .in3({ram_1_data, ram_4_data, ram_3_data, ram_2_data}), .out(multiplexer_4_out), .sel(Address[1:0]));
  and and_6 (and_6_out, Mode[0], multiplexer_2_out[7]);
  assign bit_extender_1_out = {{24{and_6_out}}, multiplexer_2_out};  // Bit_Extender bit_extender_1
  and and_7 (and_7_out, Mode[0], multiplexer_3_out[15]);
  assign bit_extender_2_out = {{16{and_7_out}}, multiplexer_3_out};  // Bit_Extender bit_extender_2
  Multiplexer #(.select(2), .width(32), .enable("false")) multiplexer_5 (
    .in0(bit_extender_1_out), .in1(bit_extender_2_out), .in2(multiplexer_4_out), .out(Data_Out),
    .sel(Mode[2:1]));  // open: in3

  // Notes on the sheet:
  //   signed
  //   byte
  //   half
  //   word
  //   1KiB Cache Line
endmodule

module L1_Cache (
  input  [15:0] Load_Data,
  input  [31:0] Load_Address,
  input  [31:0] Address,
  input  [31:0] Data_in,
  input  [2:0] Mode,
  input  Clock,
  input  Write,
  input  Enable,
  output Cache_miss,
  output [31:0] Data_Out
);

  wire cache_line_1_hit, cache_line_2_hit, cache_line_3_hit, cache_line_4_hit, cache_line_5_hit,
       cache_line_6_hit, cache_line_7_hit, cache_line_8_hit, decoder_1_out0, decoder_1_out1, decoder_1_out2,
       decoder_1_out3, decoder_1_out4, decoder_1_out5, decoder_1_out6, decoder_1_out7, not_1_out;
  wire [2:0] lru_1_oldest_address, multiplexer_3_out, priority_encoder_1_out;
  wire [31:0] bit_extender_1_out, cache_line_1_data_out, cache_line_2_data_out, cache_line_3_data_out,
       cache_line_4_data_out, cache_line_5_data_out, cache_line_6_data_out, cache_line_7_data_out,
       cache_line_8_data_out, multiplexer_1_out, multiplexer_2_out;

  Multiplexer #(.width(32), .enable("false")) multiplexer_1 (
    .in0(Address), .in1(Load_Address), .out(multiplexer_1_out), .sel(Cache_miss));
  Multiplexer #(.width(32), .enable("false")) multiplexer_2 (
    .in0(Data_in), .in1(bit_extender_1_out), .out(multiplexer_2_out), .sel(Cache_miss));
  Multiplexer #(.width(3), .enable("false")) multiplexer_3 (
    .in0(Mode), .in1(3'b010), .out(multiplexer_3_out), .sel(Cache_miss));
  assign bit_extender_1_out = {{16{1'b0}}, Load_Data};  // Bit_Extender bit_extender_1
  Decoder #(.select(3), .disabled(0)) decoder_1 (
    .out0(decoder_1_out0), .out1(decoder_1_out1), .out2(decoder_1_out2), .out3(decoder_1_out3),
    .out4(decoder_1_out4), .out5(decoder_1_out5), .out6(decoder_1_out6), .out7(decoder_1_out7),
    .sel(lru_1_oldest_address), .en(Cache_miss));
  Cache_Line cache_line_1 (
    .Write(Write), .Set_Tag(decoder_1_out0), .Clock(Clock), .Address(multiplexer_1_out),
    .Mode(multiplexer_3_out), .Data_In(multiplexer_2_out), .Hit(cache_line_1_hit),
    .Data_Out(cache_line_1_data_out), .Sel(Enable));
  Cache_Line cache_line_2 (
    .Write(Write), .Set_Tag(decoder_1_out1), .Clock(Clock), .Address(multiplexer_1_out),
    .Mode(multiplexer_3_out), .Data_In(multiplexer_2_out), .Hit(cache_line_2_hit),
    .Data_Out(cache_line_2_data_out), .Sel(Enable));
  Cache_Line cache_line_3 (
    .Write(Write), .Set_Tag(decoder_1_out2), .Clock(Clock), .Address(multiplexer_1_out),
    .Mode(multiplexer_3_out), .Data_In(multiplexer_2_out), .Hit(cache_line_3_hit),
    .Data_Out(cache_line_3_data_out), .Sel(Enable));
  Cache_Line cache_line_4 (
    .Write(Write), .Set_Tag(decoder_1_out3), .Clock(Clock), .Address(multiplexer_1_out),
    .Mode(multiplexer_3_out), .Data_In(multiplexer_2_out), .Hit(cache_line_4_hit),
    .Data_Out(cache_line_4_data_out), .Sel(Enable));
  Cache_Line cache_line_5 (
    .Write(Write), .Set_Tag(decoder_1_out4), .Clock(Clock), .Address(multiplexer_1_out),
    .Mode(multiplexer_3_out), .Data_In(multiplexer_2_out), .Hit(cache_line_5_hit),
    .Data_Out(cache_line_5_data_out), .Sel(Enable));
  Cache_Line cache_line_6 (
    .Write(Write), .Set_Tag(decoder_1_out5), .Clock(Clock), .Address(multiplexer_1_out),
    .Mode(multiplexer_3_out), .Data_In(multiplexer_2_out), .Hit(cache_line_6_hit),
    .Data_Out(cache_line_6_data_out), .Sel(Enable));
  Cache_Line cache_line_7 (
    .Write(Write), .Set_Tag(decoder_1_out6), .Clock(Clock), .Address(multiplexer_1_out),
    .Mode(multiplexer_3_out), .Data_In(multiplexer_2_out), .Hit(cache_line_7_hit),
    .Data_Out(cache_line_7_data_out), .Sel(Enable));
  Cache_Line cache_line_8 (
    .Write(Write), .Set_Tag(decoder_1_out7), .Clock(Clock), .Address(multiplexer_1_out),
    .Mode(multiplexer_3_out), .Data_In(multiplexer_2_out), .Hit(cache_line_8_hit),
    .Data_Out(cache_line_8_data_out), .Sel(Enable));
  Multiplexer #(.select(3), .width(32)) multiplexer_4 (
    .in0(cache_line_1_data_out), .in1(cache_line_2_data_out), .in2(cache_line_3_data_out),
    .in3(cache_line_4_data_out), .in4(cache_line_5_data_out), .in5(cache_line_6_data_out),
    .in6(cache_line_7_data_out), .in7(cache_line_8_data_out), .out(Data_Out), .sel(priority_encoder_1_out),
    .en(not_1_out));
  not not_1 (not_1_out, Cache_miss);
  Priority_Encoder priority_encoder_1 (
    .in0(cache_line_1_hit), .in1(cache_line_2_hit), .in2(cache_line_3_hit), .in3(cache_line_4_hit),
    .in4(cache_line_5_hit), .in5(cache_line_6_hit), .in6(cache_line_7_hit), .in7(cache_line_8_hit),
    .out(priority_encoder_1_out), .en_out(Cache_miss));  // open: en_in, gs
  LRU lru_1 (.Cache_Address(priority_encoder_1_out), .Clock(Clock), .Oldest_Address(lru_1_oldest_address));
endmodule

module conditional_increment (
  input  inc,
  input  [7:0] \input ,
  output [7:0] \output 
);

  Adder adder_1 (.a(\input ), .b({8{1'b0}}), .out(\output ), .cin(inc));  // open: cout
endmodule

module LRU (
  input  [2:0] Cache_Address,
  input  Clock,
  output [2:0] Oldest_Address
);

  wire and_1_out, and_2_out, and_3_out, and_4_out, and_5_out, and_6_out, comparator_1_eq, comparator_2_eq,
       comparator_3_eq, comparator_4_eq, comparator_5_eq, comparator_6_eq, comparator_7_eq, not_1_out,
       not_2_out, not_3_out, not_4_out, not_5_out, not_6_out, not_7_out;
  wire [2:0] register_1_q, register_2_q, register_3_q, register_4_q, register_5_q, register_6_q, register_7_q;

  Comparator #(.width(3)) comparator_1 (.a(Cache_Address), .b(register_1_q), .eq(comparator_1_eq));  // open: gt, lt
  Register #(.width(3)) register_1 (.D(Cache_Address), .en(not_1_out), .Q(register_1_q), .clk(Clock));  // open: clr
  not not_1 (not_1_out, comparator_1_eq);
  Register #(.width(3)) register_2 (.D(register_1_q), .en(not_1_out), .Q(register_2_q), .clk(Clock));  // open: clr
  Comparator #(.width(3)) comparator_2 (.a(Cache_Address), .b(register_2_q), .eq(comparator_2_eq));  // open: gt, lt
  not not_2 (not_2_out, comparator_2_eq);
  Comparator #(.width(3)) comparator_3 (.a(Cache_Address), .b(register_3_q), .eq(comparator_3_eq));  // open: gt, lt
  and and_1 (and_1_out, not_2_out, not_1_out);
  Register #(.width(3)) register_3 (.D(register_2_q), .en(and_1_out), .Q(register_3_q), .clk(Clock));  // open: clr
  not not_3 (not_3_out, comparator_3_eq);
  and and_2 (and_2_out, not_3_out, and_1_out);
  Comparator #(.width(3)) comparator_4 (.a(Cache_Address), .b(register_4_q), .eq(comparator_4_eq));  // open: gt, lt
  not not_4 (not_4_out, comparator_4_eq);
  Register #(.width(3)) register_4 (.D(register_3_q), .en(and_2_out), .Q(register_4_q), .clk(Clock));  // open: clr
  and and_3 (and_3_out, not_4_out, and_2_out);
  Register #(.width(3)) register_5 (.D(register_4_q), .en(and_3_out), .Q(register_5_q), .clk(Clock));  // open: clr
  not not_5 (not_5_out, comparator_5_eq);
  Comparator #(.width(3)) comparator_5 (.a(Cache_Address), .b(register_5_q), .eq(comparator_5_eq));  // open: gt, lt
  and and_4 (and_4_out, not_5_out, and_3_out);
  Comparator #(.width(3)) comparator_6 (.a(Cache_Address), .b(register_6_q), .eq(comparator_6_eq));  // open: gt, lt
  not not_6 (not_6_out, comparator_6_eq);
  Register #(.width(3)) register_6 (.D(register_5_q), .en(and_4_out), .Q(register_6_q), .clk(Clock));  // open: clr
  and and_5 (and_5_out, not_6_out, and_4_out);
  not not_7 (not_7_out, comparator_7_eq);
  Comparator #(.width(3)) comparator_7 (.a(Cache_Address), .b(register_7_q), .eq(comparator_7_eq));  // open: gt, lt
  Register #(.width(3)) register_7 (.D(register_6_q), .en(and_5_out), .Q(register_7_q), .clk(Clock));  // open: clr
  and and_6 (and_6_out, not_7_out, and_5_out);
  Register #(.width(3)) register_8 (.D(register_7_q), .en(and_6_out), .Q(Oldest_Address), .clk(Clock));  // open: clr
endmodule

module FIFO_256x32 (
  input  [31:0] Requested_Address,
  input  Enqueue,
  input  Dequeue,
  input  Clock,
  output Full,
  output Empty,
  output [31:0] Queue_Out
);

  wire and_1_out, and_2_out, comparator_1_eq, or_1_out, Read_Address_carry, t_ff_1_q, t_ff_2_q,
       Write_Address_carry, xor_1_out;
  wire [7:0] multiplexer_1_out, Read_Address_q, Write_Address_q;

  and and_1 (and_1_out, Enqueue, Empty, ~Full);  // AND_Gate
  and and_2 (and_2_out, Dequeue, ~Empty, Full);  // AND_Gate
  Counter Read_Address (
    .count(and_2_out), .Q(Read_Address_q), .carry(Read_Address_carry), .clk(Clock));  // open: load, D, clr
  Counter Write_Address (
    .count(and_1_out), .Q(Write_Address_q), .carry(Write_Address_carry), .clk(Clock));  // open: load, D, clr
  Multiplexer #(.width(8), .disabled(0), .enable("false")) multiplexer_1 (
    .in0(Read_Address_q), .in1(Write_Address_q), .out(multiplexer_1_out), .sel(and_1_out));
  T_Flip_Flop t_ff_1 (.clk(Clock), .T(Read_Address_carry), .Q(t_ff_1_q));  // open: Qn, preset, reset, en
  xor xor_1 (xor_1_out, t_ff_1_q, t_ff_2_q);
  T_Flip_Flop t_ff_2 (.clk(Clock), .T(Write_Address_carry), .Q(t_ff_2_q));  // open: Qn, preset, reset, en
  or or_1 (or_1_out, and_1_out, and_2_out);
  and and_3 (Full, xor_1_out, comparator_1_eq);
  and and_4 (Empty, ~xor_1_out, comparator_1_eq);  // AND_Gate
  Comparator comparator_1 (.a(Read_Address_q), .b(Write_Address_q), .eq(comparator_1_eq));  // open: gt, lt
  RAM #(.dataWidth(32), .bus("separate")) ram_1 (
    .addr(multiplexer_1_out), .din(Requested_Address), .data(Queue_Out), .str(and_1_out), .sel(or_1_out),
    .clk(Clock), .ld(and_2_out));  // open: clr
endmodule

module _32bit_increment (
  input  [31:0] In,
  output [31:0] Out
);

  Adder #(.width(32)) adder_1 (.a(In), .b({32{1'b0}}), .out(Out), .cin(1'b1));  // open: cout
endmodule

module sdram_controller (
  input  [15:0] Data_from_RAM,
  input  CAS_latency__0___2__1___3,
  input  clock,
  input  load,
  input  store,
  input  [15:0] data_in,
  input  [23:0] addr,
  input  ncs,
  output RAM_clk,
  output RAM_cke,
  output [15:0] Data_to_RAM,
  output [12:0] RAM_Address,
  output [1:0] Bank_Activate,
  output [1:0] Data_Mask,
  output RAM__cs,
  output nRAS,
  output nCAS,
  output nWE,
  output [15:0] data_out,
  output data_valid,
  output ready_to_write
);

  wire and_1_out, and_2_out, and_3_out, and_4_out, and_5_out, and_6_out, and_7_out, and_8_out, and_9_out,
       and_10_out, and_11_out, and_12_out, and_13_out, and_14_out, and_15_out, and_16_out, and_17_out,
       and_18_out, and_19_out, and_20_out, and_21_out, comparator_1_eq, comparator_2_eq, comparator_3_eq,
       comparator_4_eq, comparator_5_eq, comparator_6_eq, comparator_7_eq, comparator_8_eq, comparator_9_eq,
       comparator_10_eq, comparator_11_eq, comparator_12_eq, comparator_13_eq, comparator_14_eq,
       comparator_15_eq, comparator_16_eq, comparator_17_eq, decoder_1_out1, decoder_1_out2, decoder_1_out3,
       decoder_1_out4, decoder_1_out5, decoder_1_out6, decoder_1_out7, nand_1_out, nor_1_out, not_2_out,
       not_3_out, or_1_out, or_2_out, or_3_out, or_4_out, or_5_out, or_7_out, or_9_out, or_10_out, or_11_out,
       priority_encoder_1_gs, priority_encoder_2_en_out, request_queue_1_empty, request_queue_1_first_request;
  wire [2:0] multiplexer_1_out, priority_encoder_1_out, register_1_q;
  wire [3:0] priority_encoder_2_out;
  wire [3:3] multiplexer_5_out;
  wire [9:0] adder_1_out, adder_2_out, adder_3_out, bit_extender_2_out, statetimer_q;
  wire [10:10] or_8_out;
  wire [12:0] bit_extender_1_out, multiplexer_2_out, multiplexer_4_out;
  wire [21:0] request_queue_1_addr_of_first_request;

  and and_1 (and_1_out, request_queue_1_first_request, and_5_out, decoder_1_out1);
  Comparator #(.width(10)) comparator_1 (.a(statetimer_q), .b(10'h2), .eq(comparator_1_eq));  // open: gt, lt
  Multiplexer #(.width(3), .enable("false")) multiplexer_1 (
    .in0(3'b010), .in1(3'b011), .out(multiplexer_1_out), .sel(CAS_latency__0___2__1___3));
  request_queue request_queue_1 (
    .Read(load), .Write(store), .GetNext(and_5_out), .Clock(clock), .Empty(request_queue_1_empty),
    .First_Request(request_queue_1_first_request),
    .Addr_of_First_Request({Bank_Activate, request_queue_1_addr_of_first_request}), .Addr(addr));
  Pull_Resistor pull_resistor_1 (.node({Bank_Activate, request_queue_1_addr_of_first_request}));
  not not_1 (RAM_cke, ncs);
  and and_2 (and_2_out, decoder_1_out1, and_5_out, ~request_queue_1_first_request);  // AND_Gate
  and and_3 (and_3_out, decoder_1_out1, request_queue_1_empty);
  or or_1 (or_1_out, and_7_out, or_2_out, and_6_out);
  or or_2 (or_2_out, and_11_out, and_16_out);
  and and_4 (and_4_out, comparator_1_eq, decoder_1_out2);
  and and_5 (and_5_out, ~request_queue_1_empty, decoder_1_out1);  // AND_Gate
  Priority_Encoder priority_encoder_1 (
    .in1(or_1_out), .in2(and_1_out), .in3(and_2_out), .in4(and_3_out), .out(priority_encoder_1_out),
    .gs(priority_encoder_1_gs));  // open: in0, in5, in6, in7, en_in, en_out
  S_R_Flip_Flop write_ready (
    .S(and_4_out), .clk(clock), .R(and_11_out), .Q(ready_to_write));  // open: Qn, preset, reset, en
  S_R_Flip_Flop read_ready (
    .S(and_14_out), .clk(clock), .R(and_16_out), .Q(data_valid));  // open: Qn, preset, reset, en
  Register #(.width(3)) register_1 (
    .D(priority_encoder_1_out), .en(priority_encoder_1_gs), .Q(register_1_q), .clk(clock), .clr(or_3_out));
  or or_3 (or_3_out, decoder_1_out7, decoder_1_out6, decoder_1_out5);
  not not_2 (not_2_out, or_11_out);
  Multiplexer #(.width(13), .enable("false")) multiplexer_2 (
    .in0(request_queue_1_addr_of_first_request[21:9]), .in1(bit_extender_1_out), .out(multiplexer_2_out),
    .sel(not_2_out));
  assign bit_extender_1_out = {{4{1'b0}}, request_queue_1_addr_of_first_request[8:0]};  // Bit_Extender bit_extender_1
  Decoder #(.select(3), .disabled(0), .enable("false")) decoder_1 (
    .out0(Data_Mask[1]), .out1(decoder_1_out1), .out2(decoder_1_out2), .out3(decoder_1_out3),
    .out4(decoder_1_out4), .out5(decoder_1_out5), .out6(decoder_1_out6), .out7(decoder_1_out7),
    .sel(register_1_q));
  assign bit_extender_2_out = {{7{1'b0}}, multiplexer_1_out};  // Bit_Extender bit_extender_2
  Multiplexer #(.width(13), .enable("false")) multiplexer_3 (
    .in0(multiplexer_4_out), .in1({{6{1'b0}}, multiplexer_1_out, 4'b0111}), .out(RAM_Address),
    .sel(comparator_3_eq));
  Multiplexer #(.width(13), .enable("false")) multiplexer_4 (
    .in0(multiplexer_2_out), .in1({multiplexer_2_out[12:11], or_8_out[10], multiplexer_2_out[9:0]}),
    .out(multiplexer_4_out), .sel(or_8_out[10]));
  Counter #(.width(10), .max('h3ff)) statetimer (
    .Q(statetimer_q), .clk(clock), .clr(or_4_out));  // open: load, D, count, carry
  or or_4 (or_4_out, or_3_out, decoder_1_out1);
  Adder #(.width(10)) adder_1 (.a(bit_extender_2_out), .b(10'h2), .out(adder_1_out));  // open: cin, cout
  Adder #(.width(10)) adder_2 (.a(bit_extender_2_out), .b(10'h201), .out(adder_2_out));  // open: cin, cout
  Adder #(.width(10)) adder_3 (.a(bit_extender_2_out), .b(10'h202), .out(adder_3_out));  // open: cin, cout
  Comparator #(.width(10)) comparator_2 (.a(statetimer_q), .b(10'h1), .eq(comparator_2_eq));  // open: gt, lt
  Comparator #(.width(10)) comparator_3 (.a(statetimer_q), .b(10'h4), .eq(comparator_3_eq));  // open: gt, lt
  Comparator #(.width(10)) comparator_4 (.a(statetimer_q), .b(10'h6), .eq(comparator_4_eq));  // open: gt, lt
  Comparator #(.width(10)) comparator_5 (.a(statetimer_q), .b(10'hd), .eq(comparator_5_eq));  // open: gt, lt
  Comparator #(.width(10)) comparator_6 (.a(statetimer_q), .b(10'h11), .eq(comparator_6_eq));  // open: gt, lt
  Comparator #(.width(10)) comparator_7 (.a(statetimer_q), .b({10{1'b0}}), .eq(comparator_7_eq));  // open: gt, lt
  Comparator #(.width(10)) comparator_8 (.a(statetimer_q), .b(10'h9), .eq(comparator_8_eq));  // open: gt, lt
  Comparator #(.width(10)) comparator_9 (.a(statetimer_q), .b({10{1'b0}}), .eq(comparator_9_eq));  // open: gt, lt
  Comparator #(.width(10)) comparator_10 (.a(statetimer_q), .b(10'h3), .eq(comparator_10_eq));  // open: gt, lt
  Comparator #(.width(10)) comparator_11 (.a(statetimer_q), .b(10'h203), .eq(comparator_11_eq));  // open: gt, lt
  Comparator #(.width(10)) comparator_12 (.a(statetimer_q), .b(10'h204), .eq(comparator_12_eq));  // open: gt, lt
  Comparator #(.width(10)) comparator_13 (.a(statetimer_q), .b({10{1'b0}}), .eq(comparator_13_eq));  // open: gt, lt
  Comparator #(.width(10)) comparator_14 (.a(statetimer_q), .b(10'h3), .eq(comparator_14_eq));  // open: gt, lt
  Comparator #(.width(10)) comparator_15 (.a(statetimer_q), .b(adder_1_out), .eq(comparator_15_eq));  // open: gt, lt
  Comparator #(.width(10)) comparator_16 (.a(statetimer_q), .b(adder_2_out), .eq(comparator_16_eq));  // open: gt, lt
  Comparator #(.width(10)) comparator_17 (.a(statetimer_q), .b(adder_3_out), .eq(comparator_17_eq));  // open: gt, lt
  or or_5 (or_5_out, comparator_4_eq, comparator_5_eq);
  and and_6 (and_6_out, comparator_6_eq, Data_Mask[1]);
  and and_7 (and_7_out, comparator_8_eq, decoder_1_out4);
  and and_8 (and_8_out, decoder_1_out2, comparator_9_eq);
  and and_9 (and_9_out, decoder_1_out2, comparator_10_eq);
  and and_10 (and_10_out, decoder_1_out2, comparator_11_eq);
  and and_11 (and_11_out, decoder_1_out2, comparator_12_eq);
  and and_12 (and_12_out, comparator_13_eq, decoder_1_out3);
  and and_13 (and_13_out, comparator_14_eq, decoder_1_out3);
  and and_14 (and_14_out, comparator_15_eq, decoder_1_out3);
  and and_15 (and_15_out, comparator_16_eq, decoder_1_out3);
  and and_16 (and_16_out, comparator_17_eq, decoder_1_out3);
  nor nor_1 (nor_1_out, comparator_2_eq, comparator_3_eq, or_5_out);
  not not_3 (not_3_out, comparator_7_eq);
  or or_6 (RAM__cs, multiplexer_5_out[3], nand_1_out);
  nand nand_1 (nand_1_out, Data_Mask[1], ~nor_1_out);  // NAND_Gate
  and and_17 (and_17_out, comparator_2_eq, Data_Mask[1]);
  and and_18 (and_18_out, comparator_3_eq, Data_Mask[1]);
  and and_19 (and_19_out, or_5_out, Data_Mask[1]);
  or or_7 (or_7_out, and_19_out, and_20_out);
  and and_20 (and_20_out, decoder_1_out4, comparator_7_eq);
  and and_21 (and_21_out, decoder_1_out4, not_3_out);
  or or_8 (or_8_out[10], and_17_out, and_11_out, and_16_out);
  or or_9 (or_9_out, and_10_out, and_15_out);
  or or_10 (or_10_out, and_21_out, decoder_1_out1);
  or or_11 (or_11_out, and_8_out, and_12_out);
  Priority_Encoder #(.select(4)) priority_encoder_2 (
    .in0(and_18_out), .in1(or_7_out), .in2(or_8_out[10]), .in3(or_11_out), .in4(and_9_out), .in5(and_13_out),
    .in6(or_9_out), .in7(or_10_out), .out(priority_encoder_2_out), .en_out(priority_encoder_2_en_out));  // open: in8, in9, in10, in11, in12, in13, in14, in15, gs, en_in
  Multiplexer #(.width(4), .enable("false")) multiplexer_5 (
    .in0(priority_encoder_2_out), .in1(4'b0111), .out({multiplexer_5_out[3], nRAS, nCAS, nWE}),
    .sel(priority_encoder_2_en_out));

  assign Data_Mask[0] = Data_Mask[1];
  assign data_out = Data_from_RAM;
  assign Data_to_RAM = data_in;
  assign RAM_clk = clock;

  // Notes on the sheet:
  //   burst len
  //   init
  //   idle
  //   refresh
  //   write
  //   read
  //   cke, ldqm, udqm
  //   prechargeall
  //   setmode
  //   autorefresh
  //   exit init
  //   refresh
  //   exit refresh
  //   bank activate
  //   write
  //   burst stop
  //   precharge
  //   bank activate
  //   read
  //   data ready
  //   burst stop
  //   precharge
  //   cs#
endmodule

module request_queue (
  input  Read,
  input  Write,
  input  GetNext,
  input  Clock,
  input  [23:0] Addr,
  output Empty,
  output First_Request,
  output [23:0] Addr_of_First_Request
);

  wire and_1_out, and_2_out, and_3_out, comparator_1_eq, or_1_out, or_2_out, Read_Address_carry, t_ff_1_q,
       t_ff_2_q, Write_Address_carry, xor_1_out;
  wire [2:0] multiplexer_1_out, Read_Address_q, Write_Address_q;

  or or_1 (or_1_out, Read, Write);
  and and_1 (and_1_out, or_1_out, ~and_3_out);  // AND_Gate
  and and_2 (and_2_out, GetNext, ~Empty);  // AND_Gate
  Counter #(.width(3), .max('h7)) Read_Address (
    .count(and_2_out), .Q(Read_Address_q), .carry(Read_Address_carry), .clk(Clock));  // open: load, D, clr
  Counter #(.width(3), .max('h7)) Write_Address (
    .count(and_1_out), .Q(Write_Address_q), .carry(Write_Address_carry), .clk(Clock));  // open: load, D, clr
  Multiplexer #(.width(3), .disabled(0), .enable("false")) multiplexer_1 (
    .in0(Read_Address_q), .in1(Write_Address_q), .out(multiplexer_1_out), .sel(and_1_out));
  T_Flip_Flop t_ff_1 (.clk(Clock), .T(Read_Address_carry), .Q(t_ff_1_q));  // open: Qn, preset, reset, en
  xor xor_1 (xor_1_out, t_ff_1_q, t_ff_2_q);
  T_Flip_Flop t_ff_2 (.clk(Clock), .T(Write_Address_carry), .Q(t_ff_2_q));  // open: Qn, preset, reset, en
  or or_2 (or_2_out, and_1_out, and_2_out);
  and and_3 (and_3_out, xor_1_out, comparator_1_eq);
  and and_4 (Empty, ~xor_1_out, comparator_1_eq);  // AND_Gate
  Comparator #(.width(3)) comparator_1 (.a(Read_Address_q), .b(Write_Address_q), .eq(comparator_1_eq));  // open: gt, lt
  RAM #(.addrWidth(3), .dataWidth(25), .bus("separate")) ram_1 (
    .addr(multiplexer_1_out), .din({Write, Addr}), .data({First_Request, Addr_of_First_Request}),
    .str(and_1_out), .sel(or_2_out), .clk(Clock), .ld(and_2_out));  // open: clr
endmodule

module sdramcontroller_unit_tester (
  input  [15:0] Data_from_RAM,
  input  clock,
  output RAM_clk,
  output RAM_cke,
  output [15:0] Data_to_RAM,
  output [12:0] RAM_Address,
  output [1:0] Bank_Activate,
  output [1:0] Data_Mask,
  output RAM__cs,
  output nRAS,
  output nCAS,
  output nWE,
  output [7:0] Byte_Out,
  output byte_out_valid
);

  wire and_1_out, clock_1_out, decoder_1_out1, decoder_1_out2, decoder_1_out3, not_1_out, or_1_out,
       s_r_ff_1_qn, sdram_controller_1_data_valid, sdram_controller_1_ready_to_write;
  wire [1:0] counter_2_q;
  wire [7:0] bit_extender_1_out;
  wire [8:0] counter_1_q;
  wire [15:0] rom_1_data, sdram_controller_1_data_out;

  Clock clock_1 (.out(clock_1_out));
  or or_1 (or_1_out, sdram_controller_1_data_valid, sdram_controller_1_ready_to_write);
  Counter #(.width(9), .max('h1ff)) counter_1 (
    .count(or_1_out), .Q(counter_1_q), .clk(clock_1_out));  // open: load, D, carry, clr
  Counter #(.width(2), .max('h3)) counter_2 (
    .count(not_1_out), .Q(counter_2_q), .clk(clock_1_out));  // open: load, D, carry, clr
  Decoder #(.select(2), .enable("false")) decoder_1 (
    .out1(decoder_1_out1), .out2(decoder_1_out2), .out3(decoder_1_out3), .sel(counter_2_q));  // open: out0
  ROM #(.addrWidth(9), .dataWidth(16)) rom_1 (.addr(counter_1_q), .data(rom_1_data));  // open: sel
  not not_1 (not_1_out, decoder_1_out3);
  sdram_controller sdram_controller_1 (
    .CAS_latency__0___2__1___3(1'b1), .clock(clock_1_out), .load(decoder_1_out2), .store(decoder_1_out1),
    .data_in(rom_1_data), .data_out(sdram_controller_1_data_out), .addr({24{1'b0}}),
    .data_valid(sdram_controller_1_data_valid), .ncs(1'b0),
    .ready_to_write(sdram_controller_1_ready_to_write), .RAM_clk(RAM_clk), .RAM_cke(RAM_cke),
    .Data_from_RAM(Data_from_RAM), .Data_to_RAM(Data_to_RAM), .RAM_Address(RAM_Address),
    .Bank_Activate(Bank_Activate), .Data_Mask(Data_Mask), .RAM__cs(RAM__cs), .nRAS(nRAS), .nCAS(nCAS),
    .nWE(nWE));
  Bit_Extender #(.in_width(16), .out_width(8)) bit_extender_1 (
    .in(sdram_controller_1_data_out), .out(bit_extender_1_out));
  and and_1 (and_1_out, sdram_controller_1_data_valid, s_r_ff_1_qn);
  S_R_Flip_Flop s_r_ff_1 (
    .S(sdram_controller_1_data_valid), .clk(clock_1_out), .R(1'b0), .Q(byte_out_valid), .Qn(s_r_ff_1_qn));  // open: preset, reset, en
  Register register_1 (.D(bit_extender_1_out), .en(and_1_out), .Q(Byte_Out), .clk(clock_1_out));  // open: clr

  // Notes on the sheet:
  //   contents of rom_1 (hex, n*v repeats v):
  //   dead beef c0ff ee00
endmodule
