// Logisim project cache_rev2.circ as structural Verilog: 6 circuits, main circuit main
module main (
  input  [5:0] Address,
  input  [3:0] Data_In,
  input  Clock,
  input  Read,
  input  Write,
  input  [5:0] Ram_address,
  input  [3:0] Data_from_sdram,
  input  Read_Ready,
  output Data_out_valid,
  output [3:0] Data_Out,
  output [3:0] Data_to_sdram,
  output Miss,
  output Busy
);

  wire and_1_out, and_2_out, not_1_out, not_2_out, or_1_out, s_r_ff_2_q, s_r_ff_3_q;
  wire [3:0] tags_1_address;

  or or_1 (or_1_out, Read, Write);
  tags tags_1 (
    .New_Address(Address[5:2]), .clock(Clock), .access__read_write_enabled(or_1_out), .Miss(Miss),
    .Address(tags_1_address));  // open: Address_Valid
  and and_1 (and_1_out, Miss, or_1_out);
  S_R_Flip_Flop s_r_ff_1 (.S(Miss), .clk(Clock), .R(s_r_ff_3_q), .Q(Busy));  // open: Qn, preset, reset, en
  not not_1 (not_1_out, Read_Ready);
  and and_2 (and_2_out, Read_Ready, ~s_r_ff_2_q);  // AND_Gate
  bram bram_1 (
    .addra({tags_1_address, Address[1:0]}), .ena(not_2_out), .dina(Data_In), .wea(Write), .clka(Clock),
    .doa(Data_Out), .dob(Data_to_sdram), .addrb(Ram_address), .enb(and_1_out), .dinb(Data_from_sdram),
    .web(and_1_out), .clkb(Clock));
  not not_2 (not_2_out, and_1_out);
  S_R_Flip_Flop s_r_ff_2 (.S(Read_Ready), .clk(Clock), .R(s_r_ff_3_q), .Q(s_r_ff_2_q));  // open: Qn, preset, reset, en
  S_R_Flip_Flop s_r_ff_3 (
    .S(not_1_out), .clk(Clock), .R(and_2_out), .Q(s_r_ff_3_q), .en(s_r_ff_2_q));  // open: Qn, preset, reset
  nor nor_1 (Data_out_valid, Miss, Busy);
endmodule

module bram (
  input  [5:0] addra,
  input  ena,
  input  [3:0] dina,
  input  wea,
  input  clka,
  input  [5:0] addrb,
  input  enb,
  input  [3:0] dinb,
  input  web,
  input  clkb,
  output [3:0] doa,
  output [3:0] dob
);

  wire demultiplexer_1_out0, demultiplexer_1_out1, demultiplexer_1_out2, demultiplexer_1_out3,
       demultiplexer_2_out0, demultiplexer_2_out1, demultiplexer_2_out2, demultiplexer_2_out3;
  wire [3:0] n16x4_dualport_ram_1_doa, n16x4_dualport_ram_1_dob, n16x4_dualport_ram_2_doa,
       n16x4_dualport_ram_2_dob, n16x4_dualport_ram_3_doa, n16x4_dualport_ram_3_dob,
       n16x4_dualport_ram_4_doa, n16x4_dualport_ram_4_dob;

  Demultiplexer #(.select(2), .enable("false")) demultiplexer_1 (
    .out0(demultiplexer_1_out0), .out1(demultiplexer_1_out1), .out2(demultiplexer_1_out2),
    .out3(demultiplexer_1_out3), .in(ena), .sel(addra[5:4]));
  Demultiplexer #(.select(2), .enable("false")) demultiplexer_2 (
    .out0(demultiplexer_2_out0), .out1(demultiplexer_2_out1), .out2(demultiplexer_2_out2),
    .out3(demultiplexer_2_out3), .in(enb), .sel(addrb[5:4]));
  _16x4_dualport_ram u_16x4_dualport_ram_1 (
    .addra(addra[3:0]), .ena(demultiplexer_1_out0), .dina(dina), .wea(wea), .clka(clka), .addrb(addrb[3:0]),
    .enb(demultiplexer_2_out0), .dinb(dinb), .web(web), .clkb(clkb), .doa(n16x4_dualport_ram_1_doa),
    .dob(n16x4_dualport_ram_1_dob));
  _16x4_dualport_ram u_16x4_dualport_ram_2 (
    .addra(addra[3:0]), .ena(demultiplexer_1_out1), .dina(dina), .wea(wea), .clka(clka), .addrb(addrb[3:0]),
    .enb(demultiplexer_2_out1), .dinb(dinb), .web(web), .clkb(clkb), .doa(n16x4_dualport_ram_2_doa),
    .dob(n16x4_dualport_ram_2_dob));
  _16x4_dualport_ram u_16x4_dualport_ram_3 (
    .addra(addra[3:0]), .ena(demultiplexer_1_out2), .dina(dina), .wea(wea), .clka(clka), .addrb(addrb[3:0]),
    .enb(demultiplexer_2_out2), .dinb(dinb), .web(web), .clkb(clkb), .doa(n16x4_dualport_ram_3_doa),
    .dob(n16x4_dualport_ram_3_dob));
  _16x4_dualport_ram u_16x4_dualport_ram_4 (
    .addra(addra[3:0]), .ena(demultiplexer_1_out3), .dina(dina), .wea(wea), .clka(clka), .addrb(addrb[3:0]),
    .enb(demultiplexer_2_out3), .dinb(dinb), .web(web), .clkb(clkb), .doa(n16x4_dualport_ram_4_doa),
    .dob(n16x4_dualport_ram_4_dob));
  Multiplexer #(.select(2), .width(4), .enable("false")) multiplexer_1 (
    .in0(n16x4_dualport_ram_1_dob), .in1(n16x4_dualport_ram_2_dob), .in2(n16x4_dualport_ram_3_dob),
    .in3(n16x4_dualport_ram_4_dob), .out(dob), .sel(addrb[5:4]));
  Multiplexer #(.select(2), .width(4), .enable("false")) multiplexer_2 (
    .in0(n16x4_dualport_ram_1_doa), .in1(n16x4_dualport_ram_2_doa), .in2(n16x4_dualport_ram_3_doa),
    .in3(n16x4_dualport_ram_4_doa), .out(doa), .sel(addra[5:4]));
endmodule

module LRU16 (
  input  [3:0] slot,
  input  access,
  input  clock,
  output [3:0] oldest_slot
);

  wire and_1_out, and_2_out, and_3_out, and_4_out, and_5_out, and_6_out, and_7_out, and_8_out, and_9_out,
       and_10_out, and_11_out, and_12_out, and_13_out, and_14_out, and_15_out, comparator_1_eq,
       comparator_2_eq, comparator_3_eq, comparator_4_eq, comparator_5_eq, comparator_6_eq, comparator_7_eq,
       comparator_8_eq, comparator_9_eq, comparator_10_eq, comparator_11_eq, comparator_12_eq,
       comparator_13_eq, comparator_14_eq, comparator_15_eq, not_1_out, not_2_out, not_3_out, not_4_out,
       not_5_out, not_6_out, not_7_out, not_8_out, not_9_out, not_10_out, not_11_out, not_12_out, not_13_out,
       not_14_out, not_15_out;
  wire [3:0] register_1_q, register_2_q, register_3_q, register_4_q, register_5_q, register_6_q,
       register_7_q, register_8_q, register_9_q, register_10_q, register_11_q, register_12_q, register_13_q,
       register_14_q, register_15_q;

  Comparator #(.width(4)) comparator_1 (.a(slot), .b(register_1_q), .eq(comparator_1_eq));  // open: gt, lt
  Register #(.width(4)) register_1 (.D(slot), .en(and_1_out), .Q(register_1_q), .clk(clock));  // open: clr
  not not_1 (not_1_out, comparator_1_eq);
  and and_1 (and_1_out, access, not_1_out);
  Register #(.width(4)) register_2 (.D(register_1_q), .en(and_1_out), .Q(register_2_q), .clk(clock));  // open: clr
  Comparator #(.width(4)) comparator_2 (.a(slot), .b(register_2_q), .eq(comparator_2_eq));  // open: gt, lt
  not not_2 (not_2_out, comparator_2_eq);
  Comparator #(.width(4)) comparator_3 (.a(slot), .b(register_3_q), .eq(comparator_3_eq));  // open: gt, lt
  and and_2 (and_2_out, not_2_out, and_1_out);
  Register #(.width(4)) register_3 (.D(register_2_q), .en(and_2_out), .Q(register_3_q), .clk(clock));  // open: clr
  not not_3 (not_3_out, comparator_3_eq);
  and and_3 (and_3_out, not_3_out, and_2_out);
  Comparator #(.width(4)) comparator_4 (.a(slot), .b(register_4_q), .eq(comparator_4_eq));  // open: gt, lt
  not not_4 (not_4_out, comparator_4_eq);
  Register #(.width(4)) register_4 (.D(register_3_q), .en(and_3_out), .Q(register_4_q), .clk(clock));  // open: clr
  and and_4 (and_4_out, not_4_out, and_3_out);
  Register #(.width(4)) register_5 (.D(register_4_q), .en(and_4_out), .Q(register_5_q), .clk(clock));  // open: clr
  not not_5 (not_5_out, comparator_5_eq);
  Comparator #(.width(4)) comparator_5 (.a(slot), .b(register_5_q), .eq(comparator_5_eq));  // open: gt, lt
  and and_5 (and_5_out, not_5_out, and_4_out);
  not not_6 (not_6_out, comparator_6_eq);
  Comparator #(.width(4)) comparator_6 (.a(slot), .b(register_6_q), .eq(comparator_6_eq));  // open: gt, lt
  Register #(.width(4)) register_6 (.D(register_5_q), .en(and_5_out), .Q(register_6_q), .clk(clock));  // open: clr
  and and_6 (and_6_out, not_6_out, and_5_out);
  not not_7 (not_7_out, comparator_7_eq);
  Comparator #(.width(4)) comparator_7 (.a(slot), .b(register_7_q), .eq(comparator_7_eq));  // open: gt, lt
  Register #(.width(4)) register_7 (.D(register_6_q), .en(and_6_out), .Q(register_7_q), .clk(clock));  // open: clr
  Comparator #(.width(4)) comparator_8 (.a(slot), .b(register_8_q), .eq(comparator_8_eq));  // open: gt, lt
  and and_7 (and_7_out, not_7_out, and_6_out);
  Register #(.width(4)) register_8 (.D(register_7_q), .en(and_7_out), .Q(register_8_q), .clk(clock));  // open: clr
  not not_8 (not_8_out, comparator_8_eq);
  and and_8 (and_8_out, not_8_out, and_7_out);
  not not_9 (not_9_out, comparator_9_eq);
  Comparator #(.width(4)) comparator_9 (.a(slot), .b(register_9_q), .eq(comparator_9_eq));  // open: gt, lt
  Register #(.width(4)) register_9 (.D(register_8_q), .en(and_8_out), .Q(register_9_q), .clk(clock));  // open: clr
  and and_9 (and_9_out, not_9_out, and_8_out);
  not not_10 (not_10_out, comparator_10_eq);
  Comparator #(.width(4)) comparator_10 (.a(slot), .b(register_10_q), .eq(comparator_10_eq));  // open: gt, lt
  Register #(.width(4)) register_10 (.D(register_9_q), .en(and_9_out), .Q(register_10_q), .clk(clock));  // open: clr
  Comparator #(.width(4)) comparator_11 (.a(slot), .b(register_11_q), .eq(comparator_11_eq));  // open: gt, lt
  and and_10 (and_10_out, not_10_out, and_9_out);
  Register #(.width(4)) register_11 (.D(register_10_q), .en(and_10_out), .Q(register_11_q), .clk(clock));  // open: clr
  not not_11 (not_11_out, comparator_11_eq);
  and and_11 (and_11_out, not_11_out, and_10_out);
  not not_12 (not_12_out, comparator_12_eq);
  Comparator #(.width(4)) comparator_12 (.a(slot), .b(register_12_q), .eq(comparator_12_eq));  // open: gt, lt
  Register #(.width(4)) register_12 (.D(register_11_q), .en(and_11_out), .Q(register_12_q), .clk(clock));  // open: clr
  and and_12 (and_12_out, not_12_out, and_11_out);
  Comparator #(.width(4)) comparator_13 (.a(slot), .b(register_13_q), .eq(comparator_13_eq));  // open: gt, lt
  not not_13 (not_13_out, comparator_13_eq);
  Register #(.width(4)) register_13 (.D(register_12_q), .en(and_12_out), .Q(register_13_q), .clk(clock));  // open: clr
  Comparator #(.width(4)) comparator_14 (.a(slot), .b(register_14_q), .eq(comparator_14_eq));  // open: gt, lt
  and and_13 (and_13_out, not_13_out, and_12_out);
  Register #(.width(4)) register_14 (.D(register_13_q), .en(and_13_out), .Q(register_14_q), .clk(clock));  // open: clr
  not not_14 (not_14_out, comparator_14_eq);
  and and_14 (and_14_out, not_14_out, and_13_out);
  Comparator #(.width(4)) comparator_15 (.a(slot), .b(register_15_q), .eq(comparator_15_eq));  // open: gt, lt
  not not_15 (not_15_out, comparator_15_eq);
  Register #(.width(4)) register_15 (.D(register_14_q), .en(and_14_out), .Q(register_15_q), .clk(clock));  // open: clr
  and and_15 (and_15_out, not_15_out, and_14_out);
  Register #(.width(4)) register_16 (.D(register_15_q), .en(and_15_out), .Q(oldest_slot), .clk(clock));  // open: clr
endmodule

module tags (
  input  [3:0] New_Address,
  input  clock,
  input  access__read_write_enabled,
  output Miss,
  output [3:0] Address,
  output Address_Valid
);

  wire and_1_out, and_2_out, and_3_out, and_4_out, comparator_1_eq, comparator_2_eq, comparator_3_eq,
       decoder_1_out0, decoder_1_out1, decoder_1_out2, decoder_1_out3, not_1_out, not_2_out, not_3_out,
       priority_encoder_1_gs, priority_encoder_2_gs, tag_1_empty, tag_1_hit, tag_2_empty, tag_2_hit,
       tag_3_empty, tag_3_hit, tag_4_empty, tag_4_hit;
  wire [1:0] multiplexer_1_out, multiplexer_2_out, priority_encoder_2_out, pull_resistor_1_node,
       register_1_q, register_2_q, register_3_q, register_4_q, subtractor_1_out;
  wire [3:0] tag_1_tag_address, tag_2_tag_address, tag_3_tag_address, tag_4_tag_address;

  Multiplexer #(.width(2), .disabled(0), .enable("false")) multiplexer_1 (
    .in0(register_4_q), .in1(subtractor_1_out), .out(multiplexer_1_out), .sel(priority_encoder_1_gs));
  and and_1 (and_1_out, access__read_write_enabled, Miss);
  Decoder #(.select(2), .disabled(0)) decoder_1 (
    .out0(decoder_1_out0), .out1(decoder_1_out1), .out2(decoder_1_out2), .out3(decoder_1_out3),
    .sel(multiplexer_1_out), .en(and_1_out));
  tag tag_1 (
    .New_Address(New_Address), .select(decoder_1_out0), .Empty(tag_1_empty), .Tag_Address(tag_1_tag_address),
    .Hit(tag_1_hit), .clock(clock));
  tag tag_2 (
    .New_Address(New_Address), .select(decoder_1_out1), .Empty(tag_2_empty), .Tag_Address(tag_2_tag_address),
    .Hit(tag_2_hit), .clock(clock));
  tag tag_3 (
    .New_Address(New_Address), .select(decoder_1_out2), .Empty(tag_3_empty), .Tag_Address(tag_3_tag_address),
    .Hit(tag_3_hit), .clock(clock));
  tag tag_4 (
    .New_Address(New_Address), .select(decoder_1_out3), .Empty(tag_4_empty), .Tag_Address(tag_4_tag_address),
    .Hit(tag_4_hit), .clock(clock));
  Multiplexer #(.width(2), .enable("false")) multiplexer_2 (
    .in0(multiplexer_1_out), .in1(priority_encoder_2_out), .out(multiplexer_2_out),
    .sel(priority_encoder_2_gs));
  not not_1 (not_1_out, comparator_1_eq);
  Comparator #(.width(2)) comparator_1 (.a(multiplexer_2_out), .b(register_1_q), .eq(comparator_1_eq));  // open: gt, lt
  and and_2 (and_2_out, access__read_write_enabled, not_1_out);
  Register #(.width(2)) register_1 (.D(multiplexer_2_out), .en(and_2_out), .Q(register_1_q), .clk(clock));  // open: clr
  Comparator #(.width(2)) comparator_2 (.a(multiplexer_2_out), .b(register_2_q), .eq(comparator_2_eq));  // open: gt, lt
  not not_2 (not_2_out, comparator_2_eq);
  Register #(.width(2)) register_2 (.D(register_1_q), .en(and_2_out), .Q(register_2_q), .clk(clock));  // open: clr
  // Probe on priority_encoder_1_gs
  Pull_Resistor pull_resistor_1 (.node(pull_resistor_1_node));
  Priority_Encoder #(.select(2), .disabled(0)) priority_encoder_1 (
    .in0(tag_4_empty), .in1(tag_3_empty), .in2(tag_2_empty), .in3(tag_1_empty), .out(pull_resistor_1_node),
    .gs(priority_encoder_1_gs));  // open: en_out, en_in
  Priority_Encoder #(.select(2), .disabled(0)) priority_encoder_2 (
    .in0(tag_1_hit), .in1(tag_2_hit), .in2(tag_3_hit), .in3(tag_4_hit), .out(priority_encoder_2_out),
    .gs(priority_encoder_2_gs), .en_out(Miss));  // open: en_in
  Comparator #(.width(2)) comparator_3 (.a(multiplexer_2_out), .b(register_3_q), .eq(comparator_3_eq));  // open: gt, lt
  and and_3 (and_3_out, not_2_out, and_2_out);
  Subtractor #(.width(2)) subtractor_1 (
    .a(2'b11), .b(pull_resistor_1_node), .out(subtractor_1_out));  // open: bin, bout
  Multiplexer #(.select(2), .width(4), .disabled(0), .enable("false")) multiplexer_3 (
    .in0(tag_1_tag_address), .in1(tag_2_tag_address), .in2(tag_3_tag_address), .in3(tag_4_tag_address),
    .out(Address), .sel(multiplexer_1_out));
  not not_3 (not_3_out, comparator_3_eq);
  and and_4 (and_4_out, not_3_out, and_3_out);
  Register #(.width(2)) register_3 (.D(register_2_q), .en(and_3_out), .Q(register_3_q), .clk(clock));  // open: clr
  Register #(.width(2)) register_4 (.D(register_3_q), .en(and_4_out), .Q(register_4_q), .clk(clock));  // open: clr

  assign Address_Valid = access__read_write_enabled;
endmodule

module tag (
  input  [3:0] New_Address,
  input  select,
  input  clock,
  output Empty,
  output [3:0] Tag_Address,
  output Hit
);

  wire comparator_1_eq;

  D_Flip_Flop d_ff_1 (.clk(clock), .D(select), .Qn(Empty), .en(Empty));  // open: Q, preset, reset
  Register #(.width(4)) register_1 (.D(New_Address), .en(select), .Q(Tag_Address), .clk(clock));  // open: clr
  Comparator #(.width(4)) comparator_1 (.a(New_Address), .b(Tag_Address), .eq(comparator_1_eq));  // open: gt, lt
  and and_1 (Hit, ~Empty, comparator_1_eq);  // AND_Gate
endmodule

module I_Cache (
  input  [23:0] PC,
  input  clock,
  input  ram_clock,
  input  [31:0] ram_data,
  input  controller_override,
  output Disable_CPU,
  output [31:0] Instruction,
  output Miss
);

  wire not_1_out;
  wire [3:0] tags_1_address;

  or or_1 (Disable_CPU, controller_override, Miss);
  tags tags_1 (
    .New_Address(PC[23:20]), .clock(clock), .access__read_write_enabled(1'b1), .Miss(Miss),
    .Address(tags_1_address));  // open: Address_Valid
  not not_1 (not_1_out, controller_override);
  RAM #(.addrWidth(24), .dataWidth(32), .bus("separate")) ram_1 (
    .addr({tags_1_address, PC[19:0]}), .din(ram_data), .data(Instruction), .str(controller_override),
    .sel(1'b1), .clk(ram_clock), .ld(not_1_out));  // open: clr
endmodule
