// Logisim project cache_rev3.circ as structural Verilog: 4 circuits, main circuit main
module main (
  input  [31:0] Data_In,
  input  [31:0] Address,
  input  [1:0] Mode__byte__half__word,
  input  Read,
  input  Write,
  input  Clock,
  input  [31:0] PC,
  output [31:0] Instruction
);

  wire and_1_out, comparator_1_eq;
  wire [23:0] undriven;
  wire [31:0] multiplexer_2_out;

  Comparator #(.width(32)) comparator_1 (.a(Address), .b(PC), .eq(comparator_1_eq));  // open: gt, lt
  and and_1 (and_1_out, Write, comparator_1_eq);
  Multiplexer #(.width(32), .enable("false")) multiplexer_1 (
    .in1(multiplexer_2_out), .out(Instruction), .sel(and_1_out));  // open: in0
  Multiplexer #(.select(2), .width(32), .enable("false")) multiplexer_2 (
    .in0(Data_In), .in1({undriven, Data_In[7:0]}), .in2({undriven[23:8], Data_In[15:0]}),
    .out(multiplexer_2_out), .sel(Mode__byte__half__word));  // open: in3
  pseudoram pseudoram_1 ();  // open: Data_In, Address__16x2K, Mode__byte__half__word, read, write, clock, Data_Out
endmodule

module pseudoram (
  input  [31:0] Data_In,
  input  [14:0] Address__16x2K,
  input  [1:0] Mode__byte__half__word,
  input  read,
  input  write,
  input  clock,
  output [31:0] Data_Out
);


  assign Data_Out = {32{1'b0}};
endmodule

module tag_ram (
  input  clock,
  input  Overwrite,
  input  Access__Read___Write,
  input  [4:0] Tag_Select,
  input  [21:0] New_Tag
);

  wire and_1_out, and_2_out, and_3_out, and_4_out, and_5_out, comparator_1_eq, comparator_2_eq,
       comparator_3_eq, comparator_4_eq, nor_1_out, or_1_out, or_2_out, t_ff_1_qn, t_ff_2_qn, t_ff_3_qn,
       t_ff_4_qn;
  wire [21:0] register_1_q, register_2_q, register_3_q, register_4_q;

  LRU32 lru32_1 ();  // open: tagselect, enable, clock, lrutag
  T_Flip_Flop t_ff_1 (.clk(clock), .T(Overwrite), .Qn(t_ff_1_qn), .en(t_ff_1_qn));  // open: Q, preset, reset
  Register #(.width(22)) register_1 (.D(New_Tag), .en(Overwrite), .Q(register_1_q), .clk(clock));  // open: clr
  T_Flip_Flop t_ff_2 (.clk(clock), .T(Overwrite), .Qn(t_ff_2_qn), .en(t_ff_2_qn));  // open: Q, preset, reset
  Register #(.width(22)) register_2 (.D(New_Tag), .en(Overwrite), .Q(register_2_q), .clk(clock));  // open: clr
  T_Flip_Flop t_ff_3 (.clk(clock), .T(Overwrite), .Qn(t_ff_3_qn), .en(t_ff_3_qn));  // open: Q, preset, reset
  Register #(.width(22)) register_3 (.D(New_Tag), .en(Overwrite), .Q(register_3_q), .clk(clock));  // open: clr
  T_Flip_Flop t_ff_4 (.clk(clock), .T(Overwrite), .Qn(t_ff_4_qn), .en(t_ff_4_qn));  // open: Q, preset, reset
  Register #(.width(22)) register_4 (.D(New_Tag), .en(Overwrite), .Q(register_4_q), .clk(clock));  // open: clr
  Comparator #(.width(22)) comparator_1 (.a(register_1_q), .b(New_Tag), .eq(comparator_1_eq));  // open: gt, lt
  Comparator #(.width(22)) comparator_2 (.a(register_2_q), .b(New_Tag), .eq(comparator_2_eq));  // open: gt, lt
  Comparator #(.width(22)) comparator_3 (.a(register_3_q), .b(New_Tag), .eq(comparator_3_eq));  // open: gt, lt
  Comparator #(.width(22)) comparator_4 (.a(register_4_q), .b(New_Tag), .eq(comparator_4_eq));  // open: gt, lt
  and and_1 (and_1_out, ~t_ff_1_qn, comparator_1_eq);  // AND_Gate
  and and_2 (and_2_out, ~t_ff_2_qn, comparator_2_eq);  // AND_Gate
  and and_3 (and_3_out, ~t_ff_3_qn, comparator_3_eq);  // AND_Gate
  and and_4 (and_4_out, ~t_ff_4_qn, comparator_4_eq);  // AND_Gate
  nor nor_1 (nor_1_out, or_1_out, or_2_out);
  and and_5 (and_5_out, or_1_out, ~or_2_out);  // AND_Gate
  or or_1 (or_1_out, t_ff_1_qn, t_ff_2_qn, t_ff_3_qn, t_ff_4_qn);
  or or_2 (or_2_out, and_1_out, and_2_out, and_3_out, and_4_out);

  // Notes on the sheet:
  //   Empty
  //   Empty
  //   Empty
  //   Empty
  //   use empty
  //   Not filled
  //   Hit
  //   Hit
  //   Hit
  //   Hit
  //   use LRU
  //   Hit
endmodule

module LRU32 (
  input  [4:0] tagselect,
  input  enable,
  input  clock,
  output [4:0] lrutag
);

  wire and_1_out, and_2_out, and_3_out, and_4_out, and_5_out, and_6_out, and_7_out, and_8_out, and_9_out,
       and_10_out, and_11_out, and_12_out, and_13_out, and_14_out, and_15_out, and_16_out, and_17_out,
       and_18_out, and_19_out, and_20_out, and_21_out, and_22_out, and_23_out, and_24_out, and_25_out,
       and_26_out, and_27_out, and_28_out, and_29_out, and_30_out, and_31_out, comparator_1_eq,
       comparator_2_eq, comparator_3_eq, comparator_4_eq, comparator_5_eq, comparator_6_eq, comparator_7_eq,
       comparator_8_eq, comparator_9_eq, comparator_10_eq, comparator_11_eq, comparator_12_eq,
       comparator_13_eq, comparator_14_eq, comparator_15_eq, comparator_16_eq, comparator_17_eq,
       comparator_18_eq, comparator_19_eq, comparator_20_eq, comparator_21_eq, comparator_22_eq,
       comparator_23_eq, comparator_24_eq, comparator_25_eq, comparator_26_eq, comparator_27_eq,
       comparator_28_eq, comparator_29_eq, comparator_30_eq, comparator_31_eq;
  wire [4:0] register_1_q, register_2_q, register_3_q, register_4_q, register_5_q, register_6_q,
       register_7_q, register_8_q, register_9_q, register_10_q, register_11_q, register_12_q, register_13_q,
       register_14_q, register_15_q, register_16_q, register_17_q, register_18_q, register_19_q,
       register_20_q, register_21_q, register_22_q, register_23_q, register_24_q, register_25_q,
       register_26_q, register_27_q, register_28_q, register_29_q, register_30_q, register_31_q;

  and and_1 (and_1_out, ~comparator_1_eq, enable);  // AND_Gate
  Comparator #(.width(5)) comparator_1 (.a(tagselect), .b(register_1_q), .eq(comparator_1_eq));  // open: gt, lt
  Register #(.width(5)) register_1 (.D(tagselect), .en(and_1_out), .Q(register_1_q), .clk(clock));  // open: clr
  Register #(.width(5)) register_2 (.D(register_1_q), .en(and_1_out), .Q(register_2_q), .clk(clock));  // open: clr
  Comparator #(.width(5)) comparator_2 (.a(tagselect), .b(register_2_q), .eq(comparator_2_eq));  // open: gt, lt
  and and_2 (and_2_out, ~comparator_2_eq, and_1_out);  // AND_Gate
  Register #(.width(5)) register_3 (.D(register_2_q), .en(and_2_out), .Q(register_3_q), .clk(clock));  // open: clr
  Comparator #(.width(5)) comparator_3 (.a(tagselect), .b(register_3_q), .eq(comparator_3_eq));  // open: gt, lt
  and and_3 (and_3_out, ~comparator_3_eq, and_2_out);  // AND_Gate
  Register #(.width(5)) register_4 (.D(register_3_q), .en(and_3_out), .Q(register_4_q), .clk(clock));  // open: clr
  Comparator #(.width(5)) comparator_4 (.a(tagselect), .b(register_4_q), .eq(comparator_4_eq));  // open: gt, lt
  and and_4 (and_4_out, ~comparator_4_eq, and_3_out);  // AND_Gate
  Register #(.width(5)) register_5 (.D(register_4_q), .en(and_4_out), .Q(register_5_q), .clk(clock));  // open: clr
  Comparator #(.width(5)) comparator_5 (.a(tagselect), .b(register_5_q), .eq(comparator_5_eq));  // open: gt, lt
  and and_5 (and_5_out, ~comparator_5_eq, and_4_out);  // AND_Gate
  Register #(.width(5)) register_6 (.D(register_5_q), .en(and_5_out), .Q(register_6_q), .clk(clock));  // open: clr
  Comparator #(.width(5)) comparator_6 (.a(tagselect), .b(register_6_q), .eq(comparator_6_eq));  // open: gt, lt
  and and_6 (and_6_out, ~comparator_6_eq, and_5_out);  // AND_Gate
  Register #(.width(5)) register_7 (.D(register_6_q), .en(and_6_out), .Q(register_7_q), .clk(clock));  // open: clr
  Comparator #(.width(5)) comparator_7 (.a(tagselect), .b(register_7_q), .eq(comparator_7_eq));  // open: gt, lt
  and and_7 (and_7_out, ~comparator_7_eq, and_6_out);  // AND_Gate
  Register #(.width(5)) register_8 (.D(register_7_q), .en(and_7_out), .Q(register_8_q), .clk(clock));  // open: clr
  Comparator #(.width(5)) comparator_8 (.a(tagselect), .b(register_8_q), .eq(comparator_8_eq));  // open: gt, lt
  and and_8 (and_8_out, ~comparator_8_eq, and_7_out);  // AND_Gate
  Register #(.width(5)) register_9 (.D(register_8_q), .en(and_8_out), .Q(register_9_q), .clk(clock));  // open: clr
  Comparator #(.width(5)) comparator_9 (.a(tagselect), .b(register_9_q), .eq(comparator_9_eq));  // open: gt, lt
  and and_9 (and_9_out, ~comparator_9_eq, and_8_out);  // AND_Gate
  Register #(.width(5)) register_10 (.D(register_9_q), .en(and_9_out), .Q(register_10_q), .clk(clock));  // open: clr
  Comparator #(.width(5)) comparator_10 (.a(tagselect), .b(register_10_q), .eq(comparator_10_eq));  // open: gt, lt
  and and_10 (and_10_out, ~comparator_10_eq, and_9_out);  // AND_Gate
  Register #(.width(5)) register_11 (.D(register_10_q), .en(and_10_out), .Q(register_11_q), .clk(clock));  // open: clr
  Comparator #(.width(5)) comparator_11 (.a(tagselect), .b(register_11_q), .eq(comparator_11_eq));  // open: gt, lt
  and and_11 (and_11_out, ~comparator_11_eq, and_10_out);  // AND_Gate
  Register #(.width(5)) register_12 (.D(register_11_q), .en(and_11_out), .Q(register_12_q), .clk(clock));  // open: clr
  Comparator #(.width(5)) comparator_12 (.a(tagselect), .b(register_12_q), .eq(comparator_12_eq));  // open: gt, lt
  and and_12 (and_12_out, ~comparator_12_eq, and_11_out);  // AND_Gate
  Register #(.width(5)) register_13 (.D(register_12_q), .en(and_12_out), .Q(register_13_q), .clk(clock));  // open: clr
  Comparator #(.width(5)) comparator_13 (.a(tagselect), .b(register_13_q), .eq(comparator_13_eq));  // open: gt, lt
  and and_13 (and_13_out, ~comparator_13_eq, and_12_out);  // AND_Gate
  Register #(.width(5)) register_14 (.D(register_13_q), .en(and_13_out), .Q(register_14_q), .clk(clock));  // open: clr
  Comparator #(.width(5)) comparator_14 (.a(tagselect), .b(register_14_q), .eq(comparator_14_eq));  // open: gt, lt
  and and_14 (and_14_out, ~comparator_14_eq, and_13_out);  // AND_Gate
  Register #(.width(5)) register_15 (.D(register_14_q), .en(and_14_out), .Q(register_15_q), .clk(clock));  // open: clr
  Comparator #(.width(5)) comparator_15 (.a(tagselect), .b(register_15_q), .eq(comparator_15_eq));  // open: gt, lt
  and and_15 (and_15_out, ~comparator_15_eq, and_14_out);  // AND_Gate
  Register #(.width(5)) register_16 (.D(register_15_q), .en(and_15_out), .Q(register_16_q), .clk(clock));  // open: clr
  Comparator #(.width(5)) comparator_16 (.a(tagselect), .b(register_16_q), .eq(comparator_16_eq));  // open: gt, lt
  and and_16 (and_16_out, ~comparator_16_eq, and_15_out);  // AND_Gate
  Register #(.width(5)) register_17 (.D(register_16_q), .en(and_16_out), .Q(register_17_q), .clk(clock));  // open: clr
  Comparator #(.width(5)) comparator_17 (.a(tagselect), .b(register_17_q), .eq(comparator_17_eq));  // open: gt, lt
  and and_17 (and_17_out, ~comparator_17_eq, and_16_out);  // AND_Gate
  Register #(.width(5)) register_18 (.D(register_17_q), .en(and_17_out), .Q(register_18_q), .clk(clock));  // open: clr
  Comparator #(.width(5)) comparator_18 (.a(tagselect), .b(register_18_q), .eq(comparator_18_eq));  // open: gt, lt
  and and_18 (and_18_out, ~comparator_18_eq, and_17_out);  // AND_Gate
  Register #(.width(5)) register_19 (.D(register_18_q), .en(and_18_out), .Q(register_19_q), .clk(clock));  // open: clr
  Comparator #(.width(5)) comparator_19 (.a(tagselect), .b(register_19_q), .eq(comparator_19_eq));  // open: gt, lt
  and and_19 (and_19_out, ~comparator_19_eq, and_18_out);  // AND_Gate
  Register #(.width(5)) register_20 (.D(register_19_q), .en(and_19_out), .Q(register_20_q), .clk(clock));  // open: clr
  Comparator #(.width(5)) comparator_20 (.a(tagselect), .b(register_20_q), .eq(comparator_20_eq));  // open: gt, lt
  and and_20 (and_20_out, ~comparator_20_eq, and_19_out);  // AND_Gate
  Register #(.width(5)) register_21 (.D(register_20_q), .en(and_20_out), .Q(register_21_q), .clk(clock));  // open: clr
  Comparator #(.width(5)) comparator_21 (.a(tagselect), .b(register_21_q), .eq(comparator_21_eq));  // open: gt, lt
  and and_21 (and_21_out, ~comparator_21_eq, and_20_out);  // AND_Gate
  Register #(.width(5)) register_22 (.D(register_21_q), .en(and_21_out), .Q(register_22_q), .clk(clock));  // open: clr
  Comparator #(.width(5)) comparator_22 (.a(tagselect), .b(register_22_q), .eq(comparator_22_eq));  // open: gt, lt
  and and_22 (and_22_out, ~comparator_22_eq, and_21_out);  // AND_Gate
  Register #(.width(5)) register_23 (.D(register_22_q), .en(and_22_out), .Q(register_23_q), .clk(clock));  // open: clr
  Comparator #(.width(5)) comparator_23 (.a(tagselect), .b(register_23_q), .eq(comparator_23_eq));  // open: gt, lt
  and and_23 (and_23_out, ~comparator_23_eq, and_22_out);  // AND_Gate
  Register #(.width(5)) register_24 (.D(register_23_q), .en(and_23_out), .Q(register_24_q), .clk(clock));  // open: clr
  Comparator #(.width(5)) comparator_24 (.a(tagselect), .b(register_24_q), .eq(comparator_24_eq));  // open: gt, lt
  and and_24 (and_24_out, ~comparator_24_eq, and_23_out);  // AND_Gate
  Register #(.width(5)) register_25 (.D(register_24_q), .en(and_24_out), .Q(register_25_q), .clk(clock));  // open: clr
  Comparator #(.width(5)) comparator_25 (.a(tagselect), .b(register_25_q), .eq(comparator_25_eq));  // open: gt, lt
  and and_25 (and_25_out, ~comparator_25_eq, and_24_out);  // AND_Gate
  Register #(.width(5)) register_26 (.D(register_25_q), .en(and_25_out), .Q(register_26_q), .clk(clock));  // open: clr
  Comparator #(.width(5)) comparator_26 (.a(tagselect), .b(register_26_q), .eq(comparator_26_eq));  // open: gt, lt
  and and_26 (and_26_out, ~comparator_26_eq, and_25_out);  // AND_Gate
  Register #(.width(5)) register_27 (.D(register_26_q), .en(and_26_out), .Q(register_27_q), .clk(clock));  // open: clr
  Comparator #(.width(5)) comparator_27 (.a(tagselect), .b(register_27_q), .eq(comparator_27_eq));  // open: gt, lt
  and and_27 (and_27_out, ~comparator_27_eq, and_26_out);  // AND_Gate
  Register #(.width(5)) register_28 (.D(register_27_q), .en(and_27_out), .Q(register_28_q), .clk(clock));  // open: clr
  Comparator #(.width(5)) comparator_28 (.a(tagselect), .b(register_28_q), .eq(comparator_28_eq));  // open: gt, lt
  and and_28 (and_28_out, ~comparator_28_eq, and_27_out);  // AND_Gate
  Register #(.width(5)) register_29 (.D(register_28_q), .en(and_28_out), .Q(register_29_q), .clk(clock));  // open: clr
  Comparator #(.width(5)) comparator_29 (.a(tagselect), .b(register_29_q), .eq(comparator_29_eq));  // open: gt, lt
  and and_29 (and_29_out, ~comparator_29_eq, and_28_out);  // AND_Gate
  Register #(.width(5)) register_30 (.D(register_29_q), .en(and_29_out), .Q(register_30_q), .clk(clock));  // open: clr
  Comparator #(.width(5)) comparator_30 (.a(tagselect), .b(register_30_q), .eq(comparator_30_eq));  // open: gt, lt
  and and_30 (and_30_out, ~comparator_30_eq, and_29_out);  // AND_Gate
  Register #(.width(5)) register_31 (.D(register_30_q), .en(and_30_out), .Q(register_31_q), .clk(clock));  // open: clr
  Comparator #(.width(5)) comparator_31 (.a(tagselect), .b(register_31_q), .eq(comparator_31_eq));  // open: gt, lt
  and and_31 (and_31_out, ~comparator_31_eq, and_30_out);  // AND_Gate
  Register #(.width(5)) register_32 (.D(register_31_q), .en(and_31_out), .Q(lrutag), .clk(clock));  // open: clr
endmodule
