// Logisim project fifo.circ as structural Verilog
module fifo_asynch (
  input  [3:0] d_in,
  input  enqueue,
  input  dequeue,
  input  wclock,
  input  rclock,
  output [3:0] d_out,
  output empty,
  output full
);

  wire and_1_out, and_4_out, button_1_out, comparator_1_eq, comparator_2_eq, comparator_3_eq,
       comparator_4_eq, xnor_1_out, xor_1_out;
  wire [3:0] gray_counter_1_gray, gray_to_binary_1_binary, gray_to_binary_2_binary, grayincrement_1_out,
       register_2_q, register_3_q;
  wire [4:0] gray_counter_2_gray, register_1_q;
  wire [4:4] register_2_q_2, t_ff_1_q;

  and and_1 (and_1_out, ~full, enqueue);  // AND_Gate
  Gray_Counter gray_counter_1 (.enable(and_1_out), .clock(wclock), .clear(1'b0), .Gray(gray_counter_1_gray));
  and and_2 (full, comparator_2_eq, xor_1_out);
  // Probe on gray_to_binary_1_binary
  Gray_to_Binary gray_to_binary_1 (.Gray(gray_counter_1_gray), .Binary(gray_to_binary_1_binary));
  Comparator #(.width(4)) comparator_1 (.a(4'b1000), .b(gray_counter_1_gray), .eq(comparator_1_eq));  // open: gt, lt
  T_Flip_Flop t_ff_1 (.clk(wclock), .T(comparator_1_eq), .Q(t_ff_1_q[4]));  // open: Qn, preset, reset, en
  Comparator #(.width(4)) comparator_2 (
    .a(gray_counter_1_gray), .b(register_2_q), .eq(comparator_2_eq));  // open: gt, lt
  xor xor_1 (xor_1_out, t_ff_1_q[4], register_2_q_2[4]);
  Button button_1 (.out(button_1_out));
  _16x4_dualport_ram u_16x4_dualport_ram_1 (
    .addra(gray_to_binary_1_binary), .ena(and_1_out), .dina(d_in), .wea(1'b1), .clka(wclock),
    .addrb(gray_to_binary_2_binary), .enb(and_4_out), .dinb(4'b0000), .web(1'b0), .clkb(rclock), .dob(d_out));  // open: doa
  Register #(.width(5)) register_1 (
    .D({t_ff_1_q[4], gray_counter_1_gray}), .Q(register_1_q), .clk(rclock));  // open: en, clr
  Register #(.width(5)) register_2 (
    .D(gray_counter_2_gray), .Q({register_2_q_2[4], register_2_q}), .clk(wclock));  // open: en, clr
  grayincrement grayincrement_1 (.In(register_3_q), .Out(grayincrement_1_out));  // open: Overflow
  Register #(.width(4)) register_3 (
    .D(grayincrement_1_out), .en(button_1_out), .Q(register_3_q), .clk(button_1_out));  // open: clr
  // Probe on register_3_q
  Gray_to_Binary gray_to_binary_2 (.Gray(gray_counter_2_gray[3:0]), .Binary(gray_to_binary_2_binary));
  Gray_Counter gray_counter_2 (.enable(and_4_out), .clock(rclock), .clear(1'b0), .Gray(gray_counter_2_gray[3:0]));
  // Probe on gray_to_binary_2_binary
  Comparator #(.width(4)) comparator_3 (
    .a(4'b1000), .b(gray_counter_2_gray[3:0]), .eq(comparator_3_eq));  // open: gt, lt
  T_Flip_Flop t_ff_2 (.clk(rclock), .T(comparator_3_eq), .Q(gray_counter_2_gray[4]));  // open: Qn, preset, reset, en
  Comparator #(.width(4)) comparator_4 (
    .a(gray_counter_2_gray[3:0]), .b(register_1_q[3:0]), .eq(comparator_4_eq));  // open: gt, lt
  and and_3 (empty, comparator_4_eq, xnor_1_out);
  xnor xnor_1 (xnor_1_out, gray_counter_2_gray[4], register_1_q[4]);
  and and_4 (and_4_out, ~empty, dequeue);  // AND_Gate

  // Notes on the sheet:
  //   Write
  //   Read
endmodule

module _4x4_dualport_ram (
  input  [1:0] addra,
  input  ena,
  input  [3:0] dina,
  input  wea,
  input  clka,
  input  web,
  input  clkb,
  input  [3:0] dinb,
  input  enb,
  input  [1:0] addrb,
  output [3:0] doa,
  output [3:0] dob
);

  wire decoder_1_out0, decoder_1_out1, decoder_1_out2, decoder_1_out3, decoder_2_out0, decoder_2_out1,
       decoder_2_out2, decoder_2_out3;
  wire [1:0] controlled_buffer_5_out, controlled_buffer_6_out, controlled_buffer_7_out,
       controlled_buffer_8_out;
  wire [3:0] controlled_buffer_1_out, controlled_buffer_2_out, controlled_buffer_3_out,
       controlled_buffer_4_out, register_1_q, register_2_q, register_3_q, register_4_q;

  Decoder #(.select(2), .disabled(0)) decoder_1 (
    .out0(decoder_1_out0), .out1(decoder_1_out1), .out2(decoder_1_out2), .out3(decoder_1_out3), .sel(addra),
    .en(ena));
  assign controlled_buffer_1_out = decoder_1_out0 ? dina : 4'bz;  // Controlled_Buffer controlled_buffer_1
  assign controlled_buffer_2_out = decoder_1_out1 ? dina : 4'bz;  // Controlled_Buffer controlled_buffer_2
  assign controlled_buffer_3_out = decoder_1_out2 ? dina : 4'bz;  // Controlled_Buffer controlled_buffer_3
  assign controlled_buffer_4_out = decoder_1_out3 ? dina : 4'bz;  // Controlled_Buffer controlled_buffer_4
  assign controlled_buffer_5_out = decoder_1_out0 ? {clka, wea} : 2'bz;  // Controlled_Buffer controlled_buffer_5
  assign controlled_buffer_6_out = decoder_1_out1 ? {clka, wea} : 2'bz;  // Controlled_Buffer controlled_buffer_6
  assign controlled_buffer_7_out = decoder_1_out2 ? {clka, wea} : 2'bz;  // Controlled_Buffer controlled_buffer_7
  assign controlled_buffer_8_out = decoder_1_out3 ? {clka, wea} : 2'bz;  // Controlled_Buffer controlled_buffer_8
  assign controlled_buffer_5_out = decoder_2_out0 ? {clkb, web} : 2'bz;  // Controlled_Buffer controlled_buffer_9
  assign controlled_buffer_6_out = decoder_2_out1 ? {clkb, web} : 2'bz;  // Controlled_Buffer controlled_buffer_10
  assign controlled_buffer_7_out = decoder_2_out2 ? {clkb, web} : 2'bz;  // Controlled_Buffer controlled_buffer_11
  assign controlled_buffer_8_out = decoder_2_out3 ? {clkb, web} : 2'bz;  // Controlled_Buffer controlled_buffer_12
  assign controlled_buffer_1_out = decoder_2_out0 ? dinb : 4'bz;  // Controlled_Buffer controlled_buffer_13
  assign controlled_buffer_2_out = decoder_2_out1 ? dinb : 4'bz;  // Controlled_Buffer controlled_buffer_14
  assign controlled_buffer_3_out = decoder_2_out2 ? dinb : 4'bz;  // Controlled_Buffer controlled_buffer_15
  assign controlled_buffer_4_out = decoder_2_out3 ? dinb : 4'bz;  // Controlled_Buffer controlled_buffer_16
  Decoder #(.select(2), .disabled(0)) decoder_2 (
    .out0(decoder_2_out0), .out1(decoder_2_out1), .out2(decoder_2_out2), .out3(decoder_2_out3), .sel(addrb),
    .en(enb));
  Register #(.width(4)) register_1 (
    .D(controlled_buffer_1_out), .en(controlled_buffer_5_out[0]), .Q(register_1_q),
    .clk(controlled_buffer_5_out[1]));  // open: clr
  Register #(.width(4)) register_2 (
    .D(controlled_buffer_2_out), .en(controlled_buffer_6_out[0]), .Q(register_2_q),
    .clk(controlled_buffer_6_out[1]));  // open: clr
  Register #(.width(4)) register_3 (
    .D(controlled_buffer_3_out), .en(controlled_buffer_7_out[0]), .Q(register_3_q),
    .clk(controlled_buffer_7_out[1]));  // open: clr
  Register #(.width(4)) register_4 (
    .D(controlled_buffer_4_out), .en(controlled_buffer_8_out[0]), .Q(register_4_q),
    .clk(controlled_buffer_8_out[1]));  // open: clr
  Multiplexer #(.select(2), .width(4)) multiplexer_1 (
    .in0(register_1_q), .in1(register_2_q), .in2(register_3_q), .in3(register_4_q), .out(doa), .sel(addra),
    .en(ena));
  Multiplexer #(.select(2), .width(4)) multiplexer_2 (
    .in0(register_1_q), .in1(register_2_q), .in2(register_3_q), .in3(register_4_q), .out(dob), .sel(addrb),
    .en(enb));
endmodule

module _16x4_dualport_ram (
  input  [3:0] addra,
  input  ena,
  input  [3:0] dina,
  input  wea,
  input  clka,
  input  [3:0] addrb,
  input  enb,
  input  [3:0] dinb,
  input  web,
  input  clkb,
  output [3:0] doa,
  output [3:0] dob
);

  wire demultiplexer_1_out0, demultiplexer_1_out1, demultiplexer_1_out2, demultiplexer_1_out3,
       demultiplexer_2_out0, demultiplexer_2_out1, demultiplexer_2_out2, demultiplexer_2_out3;
  wire [3:0] n4x4_dualport_ram_1_doa, n4x4_dualport_ram_1_dob, n4x4_dualport_ram_2_doa,
       n4x4_dualport_ram_2_dob, n4x4_dualport_ram_3_doa, n4x4_dualport_ram_3_dob, n4x4_dualport_ram_4_doa,
       n4x4_dualport_ram_4_dob;

  Demultiplexer #(.select(2), .enable("false")) demultiplexer_1 (
    .out0(demultiplexer_1_out0), .out1(demultiplexer_1_out1), .out2(demultiplexer_1_out2),
    .out3(demultiplexer_1_out3), .in(ena), .sel(addra[3:2]));
  Demultiplexer #(.select(2), .enable("false")) demultiplexer_2 (
    .out0(demultiplexer_2_out0), .out1(demultiplexer_2_out1), .out2(demultiplexer_2_out2),
    .out3(demultiplexer_2_out3), .in(enb), .sel(addrb[3:2]));
  _4x4_dualport_ram u_4x4_dualport_ram_1 (
    .addra(addra[1:0]), .ena(demultiplexer_1_out0), .dina(dina), .wea(wea), .clka(clka), .web(web),
    .clkb(clkb), .dinb(dinb), .enb(demultiplexer_2_out0), .addrb(addrb[1:0]), .doa(n4x4_dualport_ram_1_doa),
    .dob(n4x4_dualport_ram_1_dob));
  _4x4_dualport_ram u_4x4_dualport_ram_2 (
    .addra(addra[1:0]), .ena(demultiplexer_1_out1), .dina(dina), .wea(wea), .clka(clka), .web(web),
    .clkb(clkb), .dinb(dinb), .enb(demultiplexer_2_out1), .addrb(addrb[1:0]), .doa(n4x4_dualport_ram_2_doa),
    .dob(n4x4_dualport_ram_2_dob));
  _4x4_dualport_ram u_4x4_dualport_ram_3 (
    .addra(addra[1:0]), .ena(demultiplexer_1_out2), .dina(dina), .wea(wea), .clka(clka), .web(web),
    .clkb(clkb), .dinb(dinb), .enb(demultiplexer_2_out2), .addrb(addrb[1:0]), .doa(n4x4_dualport_ram_3_doa),
    .dob(n4x4_dualport_ram_3_dob));
  _4x4_dualport_ram u_4x4_dualport_ram_4 (
    .addra(addra[1:0]), .ena(demultiplexer_1_out3), .dina(dina), .wea(wea), .clka(clka), .web(web),
    .clkb(clkb), .dinb(dinb), .enb(demultiplexer_2_out3), .addrb(addrb[1:0]), .doa(n4x4_dualport_ram_4_doa),
    .dob(n4x4_dualport_ram_4_dob));
  Multiplexer #(.select(2), .width(4), .enable("false")) multiplexer_1 (
    .in0(n4x4_dualport_ram_1_doa), .in1(n4x4_dualport_ram_2_doa), .in2(n4x4_dualport_ram_3_doa),
    .in3(n4x4_dualport_ram_4_doa), .out(doa), .sel(addra[3:2]));
  Multiplexer #(.select(2), .width(4), .enable("false")) multiplexer_2 (
    .in0(n4x4_dualport_ram_1_dob), .in1(n4x4_dualport_ram_2_dob), .in2(n4x4_dualport_ram_3_dob),
    .in3(n4x4_dualport_ram_4_dob), .out(dob), .sel(addrb[3:2]));
endmodule

module Gray_Counter (
  input  enable,
  input  clock,
  input  clear,
  output [3:0] Gray
);

  wire or_1_out;
  wire [2:0] counter_1_q;

  Counter #(.width(4), .max('hf)) counter_1 (
    .load(clear), .D(4'b0001), .count(enable), .Q({Gray[3], counter_1_q}), .clk(or_1_out));  // open: carry, clr
  or or_1 (or_1_out, clock, clear);
  assign Gray[2:0] = counter_1_q ^ {Gray[3], counter_1_q[2:1]};  // XOR_Gate xor_1, 3 bits wide
endmodule

module Gray_to_Binary (
  input  [3:0] Gray,
  output [3:0] Binary
);

  xor xor_1 (Binary[1], Gray[1], Binary[2]);
  xor xor_2 (Binary[2], Gray[3], Gray[2]);
  xor xor_3 (Binary[0], Gray[0], Binary[1]);

  assign Binary[3] = Gray[3];
endmodule

module grayincrement (
  input  [3:0] In,
  output [3:0] Out,
  output Overflow
);

  wire and_1_out, and_2_out, not_1_out, xor_1_out, xor_2_out, xor_3_out, xor_4_out, xor_5_out;

  xor xor_1 (xor_1_out, In[3], In[2]);
  xor xor_2 (xor_2_out, In[0], xor_3_out);
  xor xor_3 (xor_3_out, In[1], xor_1_out);
  not not_1 (not_1_out, xor_2_out);
  xor xor_4 (xor_4_out, xor_2_out, xor_3_out);
  and and_1 (and_1_out, xor_2_out, xor_3_out);
  xor xor_5 (xor_5_out, and_1_out, xor_1_out);
  and and_2 (and_2_out, and_1_out, xor_1_out);
  and and_3 (Overflow, and_2_out, In[3]);
  xor xor_6 (Out[0], not_1_out, xor_4_out);
  xor xor_7 (Out[1], xor_4_out, xor_5_out);
  xor xor_8 (Out[2], xor_5_out, Out[3]);
  xor xor_9 (Out[3], and_2_out, In[3]);
endmodule
