// Logisim project shifter.circ as structural Verilog: 1 circuit, main circuit main
module main (
  input  [4:0] shamt,
  input  [31:0] data,
  input  [4:0] shamt_2,
  input  [31:0] data_2,
  input  [4:0] shamt_3,
  input  [31:0] data_3,
  output [31:0] \output ,
  output [31:0] output_2,
  output [31:0] output_3
);

  wire [1:0] bit_extender_4_out;
  wire [3:0] bit_extender_3_out;
  wire [7:0] bit_extender_1_out;
  wire [15:0] bit_extender_2_out;
  wire [31:0] multiplexer_1_out, multiplexer_2_out, multiplexer_3_out, multiplexer_4_out, multiplexer_5_out,
       multiplexer_6_out, multiplexer_7_out, multiplexer_8_out, multiplexer_9_out, multiplexer_10_out,
       multiplexer_11_out, multiplexer_12_out;
  wire [31:31] bit_extender_5_out;

  Multiplexer #(.width(32), .disabled(0), .enable("false")) multiplexer_1 (
    .in0(data), .in1({data[15:0], {16{1'b0}}}), .out(multiplexer_1_out), .sel(shamt[4]));
  Multiplexer #(.width(32), .disabled(0), .enable("false")) multiplexer_2 (
    .in0(data_2), .in1({{16{1'b0}}, data_2[31:16]}), .out(multiplexer_2_out), .sel(shamt_2[4]));
  Multiplexer #(.width(32), .disabled(0), .enable("false")) multiplexer_3 (
    .in0(data_3), .in1({bit_extender_2_out, data_3[31:16]}), .out(multiplexer_3_out), .sel(shamt_3[4]));
  Bit_Extender #(.in_width(16), .out_width(8), .\type ("sign")) bit_extender_1 (
    .in(bit_extender_2_out), .out(bit_extender_1_out));
  assign bit_extender_2_out = {{15{data_3[31]}}, data_3[31]};  // Bit_Extender bit_extender_2
  Multiplexer #(.width(32), .disabled(0), .enable("false")) multiplexer_4 (
    .in0(multiplexer_1_out), .in1({multiplexer_1_out[23:0], {8{1'b0}}}), .out(multiplexer_4_out),
    .sel(shamt[3]));
  Multiplexer #(.width(32), .disabled(0), .enable("false")) multiplexer_5 (
    .in0(multiplexer_2_out), .in1({{8{1'b0}}, multiplexer_2_out[31:8]}), .out(multiplexer_5_out),
    .sel(shamt_2[3]));
  Multiplexer #(.width(32), .disabled(0), .enable("false")) multiplexer_6 (
    .in0(multiplexer_3_out), .in1({bit_extender_1_out, multiplexer_3_out[31:8]}), .out(multiplexer_6_out),
    .sel(shamt_3[3]));
  Bit_Extender #(.out_width(4), .\type ("sign")) bit_extender_3 (.in(bit_extender_1_out), .out(bit_extender_3_out));
  Multiplexer #(.width(32), .disabled(0), .enable("false")) multiplexer_7 (
    .in0(multiplexer_4_out), .in1({multiplexer_4_out[27:0], 4'b0000}), .out(multiplexer_7_out), .sel(shamt[2]));
  Multiplexer #(.width(32), .disabled(0), .enable("false")) multiplexer_8 (
    .in0(multiplexer_5_out), .in1({4'b0000, multiplexer_5_out[31:4]}), .out(multiplexer_8_out),
    .sel(shamt_2[2]));
  Multiplexer #(.width(32), .disabled(0), .enable("false")) multiplexer_9 (
    .in0(multiplexer_6_out), .in1({bit_extender_3_out, multiplexer_6_out[31:4]}), .out(multiplexer_9_out),
    .sel(shamt_3[2]));
  Bit_Extender #(.in_width(4), .out_width(2), .\type ("sign")) bit_extender_4 (
    .in(bit_extender_3_out), .out(bit_extender_4_out));
  Multiplexer #(.width(32), .disabled(0), .enable("false")) multiplexer_10 (
    .in0(multiplexer_7_out), .in1({multiplexer_7_out[29:0], 2'b00}), .out(multiplexer_10_out), .sel(shamt[1]));
  Multiplexer #(.width(32), .disabled(0), .enable("false")) multiplexer_11 (
    .in0(multiplexer_8_out), .in1({2'b00, multiplexer_8_out[31:2]}), .out(multiplexer_11_out),
    .sel(shamt_2[1]));
  Multiplexer #(.width(32), .disabled(0), .enable("false")) multiplexer_12 (
    .in0(multiplexer_9_out), .in1({bit_extender_4_out, multiplexer_9_out[31:2]}), .out(multiplexer_12_out),
    .sel(shamt_3[1]));
  Bit_Extender #(.in_width(2), .out_width(1), .\type ("sign")) bit_extender_5 (
    .in(bit_extender_4_out), .out(bit_extender_5_out[31]));
  Multiplexer #(.width(32), .disabled(0), .enable("false")) multiplexer_13 (
    .in0(multiplexer_10_out), .in1({multiplexer_10_out[30:0], 1'b0}), .out(\output ), .sel(shamt[0]));
  Multiplexer #(.width(32), .disabled(0), .enable("false")) multiplexer_14 (
    .in0(multiplexer_11_out), .in1({1'b0, multiplexer_11_out[31:1]}), .out(output_2), .sel(shamt_2[0]));
  Multiplexer #(.width(32), .disabled(0), .enable("false")) multiplexer_15 (
    .in0(multiplexer_12_out), .in1({bit_extender_5_out[31], multiplexer_12_out[31:1]}), .out(output_3),
    .sel(shamt_3[0]));

  // Notes on the sheet:
  //   Logical Left Shift
  //   Logical Right Shift
  //   Arithmetic Right Shift
endmodule
